# Fritzing sketch ESP8266 (saved by Fritzing 0.9.3b)
circuit board: 9.26189cm x 5.47316cm
breadboards: 1

parts:
  LCM1602_IIC1 = LCM1602 IIC [part_number="LCM1602 IIC" chip_label="LCM1602 IIC" package="DIP (Dual Inline) [THT]"]
  U1 = NodeMCU V1.0
  LCD1 = LCD screen
  U2 = SUP500F [package=sup500f]
  M1 = fc-51 [package=THT]

nets:
  VSS: LCM1602_IIC1.VSS, LCD1.VSS
  VDD: LCM1602_IIC1.VDD, LCD1.VDD
  N1: LCM1602_IIC1.V0, LCD1.V0
  N2: LCM1602_IIC1.RS, LCD1.RS
  N3: LCM1602_IIC1.RW, LCD1.R/W
  N4: LCM1602_IIC1.E, LCD1.E
  N5: LCM1602_IIC1.D0, LCD1.DB0
  N6: LCM1602_IIC1.D1, LCD1.DB1
  N7: LCM1602_IIC1.D2, LCD1.DB2
  N8: LCM1602_IIC1.D3, LCD1.DB3
  N9: LCM1602_IIC1.D4, LCD1.DB4
  N10: LCM1602_IIC1.D5, LCD1.DB5
  N11: LCM1602_IIC1.D6, LCD1.DB6
  N12: LCM1602_IIC1.D7, LCD1.DB7
  N13: LCM1602_IIC1.A, LCD1.LED+
  N14: LCM1602_IIC1.K, LCD1.LED-
  GND: LCM1602_IIC1.GND, U1.GND, U2.GND, M1.pin2
  VCC: LCM1602_IIC1.VCC, U1.3V3, U2.VCC, M1.pin3
  N15: LCM1602_IIC1.SDA, U1.D2
  N16: LCM1602_IIC1.SCL, U1.D1
  N17: U1.D3, M1.pin1
  N18: U1.D6, U2.TX-O
  N19: U1.D7, U2.RX-I

custom parts:
  LCM1602 IIC: I2C-Module to use a 1602 or 2004 LCD on with the wire.h libory Serial LCD Modul
  NodeMCU V1.0: ESP8266 based NodeMCU

// code stored in the sketch: esp.ino
#include <ESP8266WiFi.h>
#include <ESP8266HTTPClient.h>
#include <SoftwareSerial.h>
#include "TinyGPS++.h"
#include "LiquidCrystal_I2C.h"

const char *ssid = "JioFiber-ooCh7";
const char *password = "subal1234";
const char *car = "DL5SAB9876";
const char *host = "jnnsmee-2022.vercel.app";
const int httpsPort = 443;
const char *fingerprint = "D0 B6 8E BB EC 26 22 D9 2A BA D8 7F 62 E6 1A 6E 55 33 89 DE";
float mylat;
float mylon;
float D[10];

#define IRSENSOR_PIN 4
long newTime = millis();
long oldTime = millis();
bool lastRead = 0;
bool newRead = 0;
#define BLACK 0
#define WHITE 1
float Time;

TinyGPSPlus gps;
SoftwareSerial serial_connection(5, 6);

void coor()
{
    while (serial_connection.available())
    {
        gps.encode(serial_connection.read());
    }
    if (gps.location.isUpdated())
    {
        mylat = (gps.location.lat(), 6);
        mylon = (gps.location.lng(), 6);
        Serial.println(mylat);
        Serial.println(mylon);
    }
}

void msg(float speed)
{
      coor();
//    mylat = 28.6500;
//    mylon = 77.2500;
    WiFiClientSecure httpsClient;
    Serial.printf("Using fingerprint '%s'\n", fingerprint);
    httpsClient.setFingerprint(fingerprint);
    httpsClient.setTimeout(15000);
    delay(1000);

    Serial.print("HTTPS Connecting");
    int r = 0;
    while ((!httpsClient.connect(host, httpsPort)) && (r < 40))
    {
        delay(100);
        Serial.print(".");
        r++;
    }
    if (r == 40)
    {
        Serial.println("Connection failed");
    }
    else
    {
        Serial.println("Connected to web");
    }
    String Link  = "/report?car=" ;
    Link+= car ;
    Link+= "&lat="; 
    Link+= mylat ;
    Link+= "&lon="; 
    Link+= mylon ;
    Link+= "&speed=" ;
    Link+= speed;

    Serial.print("requesting URL: ");
    Serial.println(host + Link);

    httpsClient.print(String("GET ") + Link + " HTTP/1.1\r\n" +
                        "Host: " + host + "\r\n" +
                        "Connection: close\r\n\r\n");

    Serial.println("request sent");

    while (httpsClient.connected())
    {
        String line = httpsClient.readStringUntil('\n');
        if (line == "\r")
        {
            Serial.println("headers received");
            break;
        }
    }

    Serial.println("reply was:");
    Serial.println("==========");
    String line;
    while (httpsClient.available())
    {
        line = httpsClient.readStringUntil('\n');
        Serial.println(line);
    }
    Serial.println("==========");
    Serial.println("closing connection");

    delay(2000);
}

void setup()
{
    delay(1000);
    Serial.begin(115200);
    WiFi.mode(WIFI_OFF);
    delay(1000);
    WiFi.mode(WIFI_STA);

    WiFi.begin(ssid, password);
    Serial.println("");

    Serial.print("Connecting");
    while (WiFi.status() != WL_CONNECTED)
    {
        delay(500);
        Serial.print(".");
    }

    Serial.println("");
    Serial.print("Connected to ");
    Serial.println(ssid);
    Serial.print("IP address: ");
    Serial.println(WiFi.localIP());
    msg(72);
}

void loop()
{
//    newRead = digitalRead(IRSENSOR_PIN);
//    if (newRead == BLACK && newRead != lastRead)
//    {
//        lastRead = newRead;
//    }
//    if (newRead == WHITE && newRead != lastRead)
//    {
//        newTime = millis();
//        lastRead = newRead;
//        Time = (newTime - oldTime);
//        oldTime = millis();
//        float speed = (28 / Time) * 36;
//        Serial.print("Speed: " + speed);
//        if (speed > 50)
//        {
//            Serial.println("Overspeeding");
//            msg(speed);
//        }
//        else
//        {
//            Serial.println("Normal Speed");
//        }
//    }
}
