# Fritzing sketch complete sketch (saved by Fritzing 0.8.7b)
circuit board: 8.46667cm x 5.64444cm
breadboards: 1

parts:
  U1 = NodeMCU V1.0
  Part1 = Arduino Uno (Rev3) - ICSP
  LCM1602_IIC1 = LCM1602 IIC [part_number="LCM1602 IIC" chip_label="LCM1602 IIC" package="DIP (Dual Inline) [THT]"]
  U2 = SUP500F [package=sup500f]
  LCD1 = LCD screen
  M1 = fc-51 [package=THT]

nets:
  N1: U1.D2, Part1.D3_PWM, M1.pin1
  3V3: U1.3V3, U2.VCC
  GND: U1.GND, U2.GND
  N2: U1.D5, U2.RX-I
  N3: U1.D6, U2.TX-O
  N4: Part1.A4/SDA, LCM1602_IIC1.SDA
  N5: Part1.A5/SCL, LCM1602_IIC1.SCL
  5V: Part1.5V, LCM1602_IIC1.VCC, M1.pin3
  GND_2: Part1.GND, LCM1602_IIC1.GND, M1.pin2
  VSS: LCM1602_IIC1.VSS, LCD1.VSS
  VDD: LCM1602_IIC1.VDD, LCD1.VDD
  N6: LCM1602_IIC1.V0, LCD1.V0
  N7: LCM1602_IIC1.RS, LCD1.RS
  N8: LCM1602_IIC1.RW, LCD1.R/W
  N9: LCM1602_IIC1.E, LCD1.E
  N10: LCM1602_IIC1.D0, LCD1.DB0
  N11: LCM1602_IIC1.D1, LCD1.DB1
  N12: LCM1602_IIC1.D2, LCD1.DB2
  N13: LCM1602_IIC1.D3, LCD1.DB3
  N14: LCM1602_IIC1.D4, LCD1.DB4
  N15: LCM1602_IIC1.D5, LCD1.DB5
  N16: LCM1602_IIC1.D6, LCD1.DB6
  N17: LCM1602_IIC1.D7, LCD1.DB7
  N18: LCM1602_IIC1.A, LCD1.LED+
  N19: LCM1602_IIC1.K, LCD1.LED-

custom parts:
  NodeMCU V1.0: ESP8266 based NodeMCU
  LCM1602 IIC: I2C-Module to use a 1602 or 2004 LCD on with the wire.h libory Serial LCD Modul
